// Digital circuit frontpanel.dig as structural Verilog
module frontpanel (
  input  clock,
  input  erun,
  output [15:0] PC,
  output halt,
  output error
);

  wire aluopdisplay_1_p1, aluopdisplay_1_p4, aluopdisplay_1_p6, aluopdisplay_1_p7, bus, busdisplay_1_p3,
       busdisplay_1_p6, busdisplay_1_p9, busdisplay_1_p11, busdisplay_2_p3, busdisplay_2_p6, busdisplay_2_p9,
       busdisplay_2_p11, busdisplay_2_p14, busdisplay_3_p3, busdisplay_3_p6, busdisplay_3_p9,
       busdisplay_3_p11, busdisplay_3_p14, busdisplay_4_p3, busdisplay_4_p6, busdisplay_4_p9,
       busdisplay_4_p11, busdisplay_4_p14, core_1_p5, core_1_p7, core_1_p9, core_1_p11, core_1_p13,
       core_1_p15, ctrl, db, debugreg_1_p9, debugreg_1_p10, debugreg_1_p11, debugreg_1_p12, debugreg_2_p8,
       debugreg_2_p9, debugreg_2_p10, debugreg_2_p11, debugreg_2_p12, debugreg_2_p13, debugreg_3_p8,
       debugreg_3_p9, debugreg_3_p10, debugreg_3_p11, debugreg_3_p12, debugreg_3_p13, hex, instrdisplay_1_p3,
       instrdisplay_1_p5, instrdisplay_1_p7, instrdisplay_1_p9, instrdisplay_1_p11, instrdisplay_1_p13, MC,
       rddisplay_1_p3, rddisplay_1_p6, rddisplay_1_p8, rddisplay_1_p9, rddisplay_2_p1, rddisplay_2_p5,
       rddisplay_2_p6, rddisplay_2_p7, rddisplay_2_p10, rddisplay_2_p12, rddisplay_2_p13, rddisplay_3_p3,
       rddisplay_3_p6, rddisplay_3_p8, rddisplay_3_p9, \reg , run_t, skip, slow_t, stalled_t, step_t;
  wire [3:0] busdisplay_1_p2, busdisplay_1_p5, busdisplay_1_p7, busdisplay_1_p10, busdisplay_2_p2,
       busdisplay_2_p5, busdisplay_2_p7, busdisplay_2_p10, busdisplay_2_p13, busdisplay_3_p2,
       busdisplay_3_p5, busdisplay_3_p7, busdisplay_3_p10, busdisplay_3_p13, busdisplay_4_p2,
       busdisplay_4_p5, busdisplay_4_p7, busdisplay_4_p10, busdisplay_4_p13, rddisplay_2_p3;
  wire [9:0] core_1_p1;
  wire [15:0] aluopdisplay_1_p3, aluopdisplay_1_p5, instrdisplay_1_p2, instrdisplay_1_p4, instrdisplay_1_p6,
       instrdisplay_1_p8, instrdisplay_1_p10, instrdisplay_1_p12, Program_d, rddisplay_1_p2, rddisplay_1_p4,
       rddisplay_1_p7, rddisplay_2_p4, rddisplay_2_p8, rddisplay_2_p11, rddisplay_3_p2, rddisplay_3_p4,
       rddisplay_3_p7;

  BlockRAMDualPort #(.AddrBits(10), .isProgramMemory("true"), .Bits(16)) Program (
    .A(core_1_p1), .Din({16{1'b0}}), .str(1'b0), .C(MC), .D(Program_d));
  Button step (.out(step_t));
  Button slow (.out(slow_t));
  Button run (.out(run_t));
  LED stalled (.in(stalled_t));
  SixteenSeg sixteenseg_1 (.led(rddisplay_1_p2), .dp(rddisplay_1_p3));
  // rddisplay rddisplay_1: pin names not known; wires that end beside it: ctrl, rddisplay_1_p2, rddisplay_1_p3, rddisplay_1_p4, 1'b0, rddisplay_1_p6, rddisplay_1_p7, rddisplay_1_p8, rddisplay_1_p9
  // core core_1: pin names not known; wires that end beside it: core_1_p1, Program_d, MC, erun, core_1_p5, 1'b1, core_1_p7, run_t, core_1_p9, slow_t, core_1_p11, step_t, core_1_p13, clock, core_1_p15, \reg , stalled_t, skip, halt, error, db, bus, ctrl
  // datamemio datamemio_1: pin names not known; wires that end beside it: clock, core_1_p5, core_1_p7, core_1_p9, core_1_p11, core_1_p13, core_1_p15
  SixteenSeg sixteenseg_2 (.led(instrdisplay_1_p2), .dp(instrdisplay_1_p3));
  SixteenSeg sixteenseg_3 (.led(instrdisplay_1_p4), .dp(instrdisplay_1_p5));
  // instrdisplay instrdisplay_1: pin names not known; wires that end beside it: ctrl, instrdisplay_1_p2, instrdisplay_1_p3, instrdisplay_1_p4, instrdisplay_1_p5, instrdisplay_1_p6, instrdisplay_1_p7, instrdisplay_1_p8, instrdisplay_1_p9, instrdisplay_1_p10, instrdisplay_1_p11, instrdisplay_1_p12, instrdisplay_1_p13
  SixteenSeg sixteenseg_4 (.led(rddisplay_1_p4), .dp(rddisplay_1_p6));
  SixteenSeg sixteenseg_5 (.led(rddisplay_1_p7), .dp(rddisplay_1_p8));
  SixteenSeg sixteenseg_6 (.led(instrdisplay_1_p6), .dp(instrdisplay_1_p7));
  SixteenSeg sixteenseg_7 (.led(instrdisplay_1_p8), .dp(instrdisplay_1_p9));
  Seven_Seg_Hex seven_seg_hex_1 (.d(busdisplay_1_p2), .dp(busdisplay_1_p3));
  // busdisplay busdisplay_1: pin names not known; wires that end beside it: rddisplay_1_p9, busdisplay_1_p2, busdisplay_1_p3, bus, busdisplay_1_p5, busdisplay_1_p6, busdisplay_1_p7, 2'b11, busdisplay_1_p9, busdisplay_1_p10, busdisplay_1_p11, hex
  SixteenSeg sixteenseg_8 (.led(instrdisplay_1_p10), .dp(instrdisplay_1_p11));
  SixteenSeg sixteenseg_9 (.led(instrdisplay_1_p12), .dp(instrdisplay_1_p13));
  Seven_Seg_Hex seven_seg_hex_2 (.d(busdisplay_1_p5), .dp(busdisplay_1_p6));
  Seven_Seg_Hex seven_seg_hex_3 (.d(busdisplay_1_p7), .dp(busdisplay_1_p9));
  SixteenSeg sixteenseg_10 (.led(rddisplay_2_p4), .dp(rddisplay_2_p6));
  Seven_Seg_Hex seven_seg_hex_4 (.d(busdisplay_1_p10), .dp(busdisplay_1_p11));
  Seven_Seg_Hex seven_seg_hex_5 (.d(rddisplay_2_p3), .dp(rddisplay_2_p5));
  SixteenSeg sixteenseg_11 (.led(rddisplay_2_p8), .dp(rddisplay_2_p10));
  SixteenSeg sixteenseg_12 (.led(rddisplay_2_p11), .dp(rddisplay_2_p12));
  // rddisplay rddisplay_2: pin names not known; wires that end beside it: rddisplay_2_p1, rddisplay_2_p1, rddisplay_2_p3, rddisplay_2_p4, rddisplay_2_p5, rddisplay_2_p6, rddisplay_2_p7, rddisplay_2_p8, 1'b1, rddisplay_2_p10, rddisplay_2_p11, rddisplay_2_p12, rddisplay_2_p13
  Seven_Seg_Hex seven_seg_hex_6 (.d(busdisplay_2_p2), .dp(busdisplay_2_p3));
  // busdisplay busdisplay_2: pin names not known; wires that end beside it: rddisplay_2_p7, busdisplay_2_p2, busdisplay_2_p3, bus, busdisplay_2_p5, busdisplay_2_p6, busdisplay_2_p7, 2'b01, busdisplay_2_p9, busdisplay_2_p10, busdisplay_2_p11, hex, busdisplay_2_p13, busdisplay_2_p14
  SixteenSeg sixteenseg_13 (.led(rddisplay_3_p2), .dp(rddisplay_3_p3));
  Seven_Seg_Hex seven_seg_hex_7 (.d(busdisplay_2_p5), .dp(busdisplay_2_p6));
  Seven_Seg_Hex seven_seg_hex_8 (.d(busdisplay_2_p7), .dp(busdisplay_2_p9));
  // debugreg debugreg_1: pin names not known; wires that end beside it: 5'b10001, {5{1'b0}}, 5'b01101, 5'b01110, 5'b01111, {5{1'b0}}, \reg , PC, debugreg_1_p9, debugreg_1_p10, debugreg_1_p11, debugreg_1_p12
  SixteenSeg sixteenseg_14 (.led(rddisplay_3_p4), .dp(rddisplay_3_p6));
  SixteenSeg sixteenseg_15 (.led(rddisplay_3_p7), .dp(rddisplay_3_p8));
  // rddisplay rddisplay_3: pin names not known; wires that end beside it: rddisplay_2_p13, rddisplay_3_p2, rddisplay_3_p3, rddisplay_3_p4, 1'b0, rddisplay_3_p6, rddisplay_3_p7, rddisplay_3_p8, rddisplay_3_p9
  Seven_Seg_Hex seven_seg_hex_9 (.d(busdisplay_2_p10), .dp(busdisplay_2_p11));
  Seven_Seg_Hex seven_seg_hex_10 (.d(busdisplay_2_p13), .dp(busdisplay_2_p14));
  // Probe RA on debugreg_1_p9
  // Probe FP on debugreg_1_p10
  // Probe BP on debugreg_1_p11
  // Probe SP on debugreg_1_p12
  Seven_Seg_Hex seven_seg_hex_11 (.d(busdisplay_3_p2), .dp(busdisplay_3_p3));
  SixteenSeg sixteenseg_16 (.led(aluopdisplay_1_p3), .dp(aluopdisplay_1_p4));
  // aluopdisplay aluopdisplay_1: pin names not known; wires that end beside it: aluopdisplay_1_p1, aluopdisplay_1_p1, aluopdisplay_1_p3, aluopdisplay_1_p4, aluopdisplay_1_p5, aluopdisplay_1_p6, aluopdisplay_1_p7
  Seven_Seg_Hex seven_seg_hex_12 (.d(busdisplay_3_p5), .dp(busdisplay_3_p6));
  Seven_Seg_Hex seven_seg_hex_13 (.d(busdisplay_3_p7), .dp(busdisplay_3_p9));
  // busdisplay busdisplay_3: pin names not known; wires that end beside it: rddisplay_3_p9, busdisplay_3_p2, busdisplay_3_p3, bus, busdisplay_3_p5, busdisplay_3_p6, busdisplay_3_p7, 2'b00, busdisplay_3_p9, busdisplay_3_p10, busdisplay_3_p11, hex, busdisplay_3_p13, busdisplay_3_p14
  SixteenSeg sixteenseg_17 (.led(aluopdisplay_1_p5), .dp(aluopdisplay_1_p6));
  // debugreg debugreg_2: pin names not known; wires that end beside it: 5'b00001, 5'b00010, 5'b00011, 5'b00100, 5'b00101, 5'b00110, \reg , debugreg_2_p8, debugreg_2_p9, debugreg_2_p10, debugreg_2_p11, debugreg_2_p12, debugreg_2_p13
  Seven_Seg_Hex seven_seg_hex_14 (.d(busdisplay_3_p10), .dp(busdisplay_3_p11));
  Seven_Seg_Hex seven_seg_hex_15 (.d(busdisplay_3_p13), .dp(busdisplay_3_p14));
  Seven_Seg_Hex seven_seg_hex_16 (.d(busdisplay_4_p2), .dp(busdisplay_4_p3));
  Seven_Seg_Hex seven_seg_hex_17 (.d(busdisplay_4_p5), .dp(busdisplay_4_p6));
  // busdisplay busdisplay_4: pin names not known; wires that end beside it: aluopdisplay_1_p7, busdisplay_4_p2, busdisplay_4_p3, bus, busdisplay_4_p5, busdisplay_4_p6, busdisplay_4_p7, 2'b10, busdisplay_4_p9, busdisplay_4_p10, busdisplay_4_p11, hex, busdisplay_4_p13, busdisplay_4_p14
  // Probe R1_a0 on debugreg_2_p8
  // Probe R2_a1 on debugreg_2_p9
  // Probe R3_a2 on debugreg_2_p10
  // Probe R4_s0 on debugreg_2_p11
  // Probe R5_s1 on debugreg_2_p12
  // Probe R6_s2 on debugreg_2_p13
  Seven_Seg_Hex seven_seg_hex_18 (.d(busdisplay_4_p7), .dp(busdisplay_4_p9));
  Seven_Seg_Hex seven_seg_hex_19 (.d(busdisplay_4_p10), .dp(busdisplay_4_p11));
  Seven_Seg_Hex seven_seg_hex_20 (.d(busdisplay_4_p13), .dp(busdisplay_4_p14));
  // debugreg debugreg_3: pin names not known; wires that end beside it: 5'b00111, 5'b01000, 5'b01001, 5'b01010, 5'b01011, 5'b01100, \reg , debugreg_3_p8, debugreg_3_p9, debugreg_3_p10, debugreg_3_p11, debugreg_3_p12, debugreg_3_p13
  // Probe R7_s3 on debugreg_3_p8
  // Probe R8_t0 on debugreg_3_p9
  // Probe R9_t1 on debugreg_3_p10
  // Probe R10_t2 on debugreg_3_p11
  // Probe R11_t3 on debugreg_3_p12
  // Probe R12_t4 on debugreg_3_p13
  DipSwitch u_hex (.out(hex));
  LED u_skip (.in(skip));

  // Other names for the same wires on the sheet: C = clock

  // Notes on the sheet:
  //   clock: Hz: 2147483647
  //   rj45 Creates
  //   =
endmodule
